# Fritzing sketch Fritzing Teensy 3D Audio (saved by Fritzing 0.9.3b)
breadboards: 1

parts:
  Teensy_3_1 = Teensy 3.1
  S1 = Pushbutton [package="[THT]"]
  S2 = Pushbutton [package="[THT]"]
  Part1 = Thumb Joystick
  Part2 = Bluetooth Mate Silver
  BAT2 = Battery Holders [package=battcom_20mm_pth]
  S3 = SPST Switch [package=switch-spdt_kit]
  S4 = Round Pushbutton

nets:
  N1: Teensy_3_1.GND, BAT2.-
  N2: Teensy_3_1.D0, Part2.TX-O
  N3: Teensy_3_1.D1, Part2.RX-I
  N4: Teensy_3_1.A6/D20, S4.leg1
  N5: Teensy_3_1.3V3, S3.O
  N6: Teensy_3_1.Vin, BAT2.+
  GND: S1.Pin_3, S1.Pin_4, S2.Pin_3, S2.Pin_4, Part1.GND, Part2.GND, S4.leg0
  N7: Part1.VERT, Part1.VCC

custom parts:
  Bluetooth Mate Silver: Description: The Bluetooth Mate is very similar to our BlueSMiRF modem, but it is designed specifically to be used with our Arduino Pros and LilyPad Arduinos. These modems work as a serial (RX/TX) pipe, and are a great wireless replacement for serial cables. Any serial stream from 9600 to 115200bps can be passed seamlessly from your computer to your target. Bluetooth Mate has the same pin out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
